# Fritzing sketch ExampleSketch (saved by Fritzing 0.9.4)
breadboards: 1

parts:
  Raspberry_Pi_1 = WaziDev 1.4 [part_number=WAZIDEV-V1.4]
  LED1 = RGB LED (com. anode, rbg) [package="5 mm [THT]"]
  RHT1 = Humidity and Temperature Sensor RHT03
  R1 = Resistor [tolerance=±5% resistance=220 package="0805 [SMD]"]
  R2 = Resistor [tolerance=±5% resistance=220 package="0805 [SMD]"]
  R3 = Resistor [tolerance=±5% resistance=220 package="0805 [SMD]"]

nets:
  N1: Raspberry_Pi_1.D6, RHT1.Data-signal
  N2: Raspberry_Pi_1.D9, R3.Pin_1
  N3: Raspberry_Pi_1.D10, R2.Pin_1
  N4: Raspberry_Pi_1.D11, R1.Pin_1
  VCC: Raspberry_Pi_1.VCC, RHT1.Vcc
  N5: Raspberry_Pi_1.GND, LED1.common_anode, RHT1.GND_2
  N6: LED1.red_cathode, R1.Pin_0
  N7: LED1.blue_cathode, R2.Pin_0
  N8: LED1.green_cathode, R3.Pin_0

custom parts:
  WaziDev 1.4: WaziDev is a Sensing and Actuation platform for your applications! It can send your data up to 7 Km using the LoRa technology. It is easily programmable and customizable, using Arduino technology. It is an ideal solution for start-ups and entrepreneurs who want to rapid prototype a IoT applications.
